// Logisim project flipflop.circ as structural Verilog: 1 circuit, main circuit main
module main (
  input  Data,
  output Q,
  output nQ
);

  wire clock_1_out, nand_1_out, nand_2_out, nand_3_out, nand_4_out, nand_5_out, nand_6_out, not_1_out;

  Clock clock_1 (.out(clock_1_out));
  nand nand_1 (nand_1_out, Data, clock_1_out);
  nand nand_2 (nand_2_out, nand_1_out, clock_1_out);
  not not_1 (not_1_out, clock_1_out);
  nand nand_3 (nand_3_out, nand_1_out, nand_4_out);
  nand nand_4 (nand_4_out, nand_3_out, nand_2_out);
  nand nand_5 (nand_5_out, nand_3_out, not_1_out);
  nand nand_6 (nand_6_out, not_1_out, nand_4_out);
  nand nand_7 (Q, nand_5_out, nQ);
  nand nand_8 (nQ, Q, nand_6_out);

  // Notes on the sheet:
  //   CLK
  //   Master Latch
  //   Slave Latch
endmodule
